# Fritzing sketch display (saved by Fritzing 0.9.6b)
breadboards: 1

parts:
  Part1 = Arduino Nano (Rev3.0)
  U2 = MAX7219 [package=dil24]  # not connected
  Part2 = MAX7219 8x8 LedMatrix Module
  U3 = 7-SEGMENT-4DIGIT [package=7-segment-4digit]  # not connected
  U4 = 7-SEGMENT-4DIGIT [package=7-segment-4digit]  # not connected

nets:
  GND: Part1.GND, Part2.GND
  N1: Part1.D10, Part2.CS
  N2: Part1.D11/MOSI, Part2.DIN
  5V: Part1.5V, Part2.VCC
  N3: Part1.D13/SCK, Part2.CLK

custom parts:
  MAX7219 8x8 LedMatrix Module: Description: MAX7219 8x8 LedMatrix Red Module Dimensions: 32x32mm Documents:
