# Fritzing sketch keypad (saved by Fritzing 0.9.6b)
breadboards: 1

parts:
  Part1 = Arduino Nano (Rev3.0)
  U1 = SN74LS20N [package="DIP14 [THT]"]
  Keypad4x1 = Keypad Membran 4x4

nets:
  GND: Part1.GND, U1.GND
  N1: Part1.D3, U1.2Y
  N2: Part1.D4, Keypad4x1.Pin1
  N3: Part1.D5, Keypad4x1.Pin2
  N4: Part1.D6, Keypad4x1.Pin3
  N5: Part1.D7, Keypad4x1.Pin4
  5V: Part1.5V, U1.VCC
  N6: Part1.A3, U1.2A, Keypad4x1.Pin8
  N7: Part1.A2, U1.2B, Keypad4x1.Pin7
  N8: Part1.A1, U1.2C, Keypad4x1.Pin6
  N9: Part1.A0, U1.2D, Keypad4x1.Pin5

custom parts:
  Keypad Membran 4x4: Membrane Keypad 4x4 Matrix
