# Fritzing sketch CowPi-mk1c-nano-i2c-lcd1602 (saved by Fritzing 0.9.9b)
breadboards: 1

parts:
  Part1 = Arduino Nano (Rev3.0)
  R1 = Resistor [tolerance=±5% power=0.25 resistance=1k package=THT]
  LED1 = LED - 5mm [color="Red (633nm)" current=0.030 package="5 mm [THT]"]
  U2 = SN74LS20N [package="DIP14 [THT]"]
  S1 = Toggle Switch [package=THT]
  S2 = Toggle Switch [package=THT]
  Keypad4x1 = Keypad Membran 4x4
  S6 = Momentary Switch 6mm 2pin
  S7 = Pushbutton [package="[THT]"]
  LCM1602_IIC1 = LCM1602 IIC [part_number="LCM1602 IIC" chip_label="LCM1602 IIC" package="DIP (Dual Inline) [THT]"]
  LCD1 = LCD screen

nets:
  GND: Part1.GND, Part1.A4, LED1.cathode, U2.GND, S1.L1, S2.L1, S6.2, S7.Pin_1, S7.Pin_2, LCM1602_IIC1.GND, LCM1602_IIC1.SDA
  N1: Part1.D2, U2.1Y
  N2: Part1.D3, U2.2Y
  N3: Part1.D4, Keypad4x1.Pin1
  N4: Part1.D5, Keypad4x1.Pin2
  N5: Part1.D6, Keypad4x1.Pin3
  N6: Part1.D7, Keypad4x1.Pin4
  N7: Part1.D8, U2.1B, S6.1
  N8: Part1.D9, U2.1A, S7.Pin_3, S7.Pin_4
  N9: Part1.D10, S2.COM
  N10: Part1.D11/MOSI, S1.COM
  N11: Part1.D12/MISO, R1.Pin_0
  VCC: Part1.5V, U2.1C, U2.1D, U2.VCC, LCM1602_IIC1.VCC
  N12: Part1.A5, LCM1602_IIC1.SCL
  N13: Part1.A3, U2.2A, Keypad4x1.Pin8
  N14: Part1.A2, U2.2B, Keypad4x1.Pin7
  N15: Part1.A1, U2.2C, Keypad4x1.Pin6
  N16: Part1.A0, U2.2D, Keypad4x1.Pin5
  N17: R1.Pin_1, LED1.anode
  VSS: LCM1602_IIC1.VSS, LCD1.VSS
  VDD: LCM1602_IIC1.VDD, LCD1.VDD
  N18: LCM1602_IIC1.V0, LCD1.V0
  N19: LCM1602_IIC1.RS, LCD1.RS
  N20: LCM1602_IIC1.RW, LCD1.R/W
  N21: LCM1602_IIC1.E, LCD1.E
  N22: LCM1602_IIC1.D0, LCD1.DB0
  N23: LCM1602_IIC1.D1, LCD1.DB1
  N24: LCM1602_IIC1.D2, LCD1.DB2
  N25: LCM1602_IIC1.D3, LCD1.DB3
  N26: LCM1602_IIC1.D4, LCD1.DB4
  N27: LCM1602_IIC1.D5, LCD1.DB5
  N28: LCM1602_IIC1.D6, LCD1.DB6
  N29: LCM1602_IIC1.D7, LCD1.DB7
  N30: LCM1602_IIC1.A, LCD1.LED+
  N31: LCM1602_IIC1.K, LCD1.LED-

custom parts:
  Keypad Membran 4x4: Membrane Keypad 4x4 Matrix
  Momentary Switch 6mm 2pin: Momentary Switch 6mm 2 pin Button commonly used for reset or general input.
  LCM1602 IIC: I2C-Module to use a 1602 or 2004 LCD on with the wire.h libory Serial LCD Modul
