# Fritzing sketch pushbutton (saved by Fritzing 0.9.6b)
breadboards: 1

parts:
  Part1 = Arduino Nano (Rev3.0)
  U1 = SN74LS20N [package="DIP14 [THT]"]
  S1 = Pushbutton [package=THT]
  S2 = Pushbutton [package=THT]

nets:
  GND: Part1.GND, U1.GND, S1.leg1, S2.leg1
  N1: Part1.D2, U1.1Y
  N2: Part1.D8, U1.1B, S1.leg0
  N3: Part1.D9, U1.1A, S2.leg0
  5V: Part1.5V, U1.1C, U1.1D, U1.VCC
