# Fritzing sketch switch-original (saved by Fritzing 0.9.6b)
breadboards: 1

parts:
  Part1 = Arduino Nano (Rev3.0)
  U1 = SN74LS20N [package="DIP14 [THT]"]
  S1 = Toggle Switch [package=THT]
  S2 = Toggle Switch [package=THT]

nets:
  GND: Part1.GND, U1.GND, S1.L1, S2.L1
  5V: Part1.5V, U1.VCC, S1.L2, S2.L2
  N1: Part1.A5, S2.COM
  N2: Part1.A4, S1.COM
