# Fritzing sketch led (saved by Fritzing 0.9.6b)
breadboards: 1

parts:
  Part1 = Arduino Nano (Rev3.0)
  R1 = Resistor [tolerance=±5% power=0.25 resistance=1k package=THT]
  LED1 = LED - 5mm [color="Red (633nm)" current=0.030 package="5 mm [THT]"]

nets:
  N1: Part1.GND, LED1.cathode
  N2: Part1.D12/MISO, R1.Pin_0
  N3: R1.Pin_1, LED1.anode
