# Fritzing sketch experimental (saved by Fritzing 0.9.9b)
breadboards: 3

parts:
  Part1 = Arduino Nano (Rev3.0)
  R1 = Resistor [tolerance=±5% power=0.25 resistance=1k package=THT]
  LED1 = LED - 5mm [color="Red (633nm)" current=0.030 package="5 mm [THT]"]
  U2 = SN74LS20N [package="DIP14 [THT]"]
  S1 = Toggle Switch [package=THT]
  S2 = Toggle Switch [package=THT]
  Keypad4x1 = Keypad Membran 4x4
  U3 = 74HC595 SMD [package="SO16 [SMD]"]  # not connected
  LCD1 = LCD screen  # not connected
  R2 = Trimmer Potentiometer [maximum_resistance=10kΩ package=THT]  # not connected
  S3 = Momentary Switch 6mm 2pin
  S4 = Momentary Switch 6mm 2pin
  Part2 = Arduino Nano Every
  M1 = Arduino Nano 33 IOT-tht  # not connected
  Q1 = TRANSISTOR_NPN [package=to-92]  # not connected
  U4 = SN74LS20N [package="DIP14 [THT]"]
  S5 = Pushbutton [package="[THT]"]
  S6 = Pushbutton [package="[THT]"]
  LCM1602_IIC1 = LCM1602 IIC [part_number="LCM1602 IIC" chip_label="LCM1602 IIC" package="DIP (Dual Inline) [THT]"]
  U5 = LCD-16X2 [package=lcd-16x2]
  U6 = SN74LS20N [package="DIP14 [THT]"]
  Keypad4x2 = Keypad Membran 4x4  # not connected
  S7 = Momentary Switch 6mm 2pin
  S8 = Momentary Switch 6mm 2pin
  S9 = Toggle Switch [package=THT]  # not connected
  S10 = Toggle Switch [package=THT]  # not connected

nets:
  GND: Part1.GND, LED1.cathode, U2.GND, S1.COM, S2.COM, S3.2, S4.2
  N1: Part1.D2, U2.1Y
  N2: Part1.D3, U2.2Y
  N3: Part1.D4, Keypad4x1.Pin1
  N4: Part1.D5, Keypad4x1.Pin2
  N5: Part1.D6, Keypad4x1.Pin3
  N6: Part1.D7, Keypad4x1.Pin4
  N7: Part1.D8, U2.1D, S4.1
  N8: Part1.D9, U2.1A, S3.1
  N9: Part1.D12/MISO, R1.Pin_0
  N10: Part1.5V, U2.1B, U2.1C
  N11: Part1.A5, S2.L1
  N12: Part1.A4, S1.L1
  N13: Part1.A3, U2.2A, Keypad4x1.Pin8
  N14: Part1.A2, U2.2B, Keypad4x1.Pin7
  N15: Part1.A1, U2.2C, Keypad4x1.Pin6
  N16: Part1.A0, U2.2D, Keypad4x1.Pin5
  N17: R1.Pin_1, LED1.anode
  N18: Part2.RESET, Part2.A7
  N19: Part2.GND, Part2.D13~
  N20: Part2.D11/MOSI, Part2.+5V
  N21: U4.1B, S6.Pin_1, S6.Pin_2
  N22: U4.NC#2, S5.Pin_3, S5.Pin_4
  N23: U4.1D, S5.Pin_1, S5.Pin_2
  N24: S6.Pin_3, S6.Pin_4
  VSS: LCM1602_IIC1.VSS, U5.VSS
  VDD: LCM1602_IIC1.VDD, U5.VDD
  N25: LCM1602_IIC1.V0, U5.VO
  N26: LCM1602_IIC1.RS, U5.RS
  N27: LCM1602_IIC1.RW, U5.R_W
  N28: LCM1602_IIC1.E, U5.E
  N29: LCM1602_IIC1.D0, U5.DB0
  N30: LCM1602_IIC1.D1, U5.DB1
  N31: LCM1602_IIC1.D2, U5.DB2
  N32: LCM1602_IIC1.D3, U5.DB3
  N33: LCM1602_IIC1.D4, U5.DB4
  N34: LCM1602_IIC1.D5, U5.DB5
  N35: LCM1602_IIC1.D6, U5.DB6
  N36: LCM1602_IIC1.D7, U5.DB7
  N37: LCM1602_IIC1.A, U5.A
  N38: LCM1602_IIC1.K, U5.K
  N39: U6.1A, S8.2
  N40: U6.1C, S7.2

custom parts:
  Keypad Membran 4x4: Membrane Keypad 4x4 Matrix
  Momentary Switch 6mm 2pin: Momentary Switch 6mm 2 pin Button commonly used for reset or general input.
  Arduino Nano Every: The Nano Every is Arduino’s 5V compatible board in the smallest available form factor: 45x18mm! The Arduino Nano is the preferred board for many projects requiring a small and easy to use microcontroller board. The small footprint and low price, make the Nano Every particularly suited for wearable inventions, low cost robotics, electronic musical instruments, and general use to control smaller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
  Arduino Nano 33 IOT-tht: The Arduino Nano 33 IoT is the easiest and cheapest point of entry to enhance existing devices (and creating new ones) to be part of the IoT and designing pico-network applications. Whether you are looking at building a sensor network connected to your office or home router, or if you want to create a BLE device sending data to a cellphone, the Nano 33 IoT is your one-stop-solution for many of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
  LCM1602 IIC: I2C-Module to use a 1602 or 2004 LCD on with the wire.h libory Serial LCD Modul
