# Fritzing sketch nand (saved by Fritzing 0.9.6b)
breadboards: 1

parts:
  Part1 = Arduino Nano (Rev3.0)
  U1 = SN74LS20N [package="DIP14 [THT]"]

nets:
  GND: Part1.GND, U1.GND
  N1: Part1.D2, U1.1Y
  N2: Part1.D3, U1.2Y
  5V: Part1.5V, U1.VCC
